# Fritzing sketch Desk_buddy_Scheme (saved by Fritzing 0.9.3b)

parts:
  Pro_Trinket_5v = Adafruit Pro Trinket 5V 16MHz [part_number="Adafruit #2000"]
  MAX4466 = Adafruit MAX4466 Electret Microphone Amplifier [part_number="Adafruit #1063"]
  Part1 = HY-SRF05 Ultrasonic Rangefinder
  Part2 = Adafruit AT42QT1012 Standalone Toggle Capacitive Touch Sensor Breakout [part_number="Adafruit #1375"]
  IC1 = Voltage Regulator [package=to-220-alt]
  VCC1 = Battery block 9V
  Part4 = NRF24L01+ Breakout Board
  BAT1 = Battery Holders [package=battcom_20mm_pth]

nets:
  GND: Pro_Trinket_5v.GND, MAX4466.GND, Part1.GND, Part2.GND, IC1.IN, VCC1.-
  N1: Pro_Trinket_5v.VBAT, IC1.OUT
  VCC: Pro_Trinket_5v.+5V, MAX4466.VCC, Part1.Vcc, Part2.VDD
  N2: Pro_Trinket_5v.D6, Part1.Echo
  N3: Pro_Trinket_5v.D5, Part1.Trig
  N4: Pro_Trinket_5v.D4, Part2.OUT
  N5: Pro_Trinket_5v.D9, Part4.CS
  N6: Pro_Trinket_5v.D10, Part4.CE
  N7: Pro_Trinket_5v.D11, Part4.MOSI
  N8: Pro_Trinket_5v.D12, Part4.MISO
  N9: Pro_Trinket_5v.D13, Part4.SCK
  N10: Pro_Trinket_5v.A0, MAX4466.OUT
  N11: IC1.GND, VCC1.+
  N12: Part4.GND, BAT1.-
  N13: Part4.VCC, BAT1.+

notes:
  Change this into a push button // sfill the hole with the wood putty

custom parts:
  Adafruit Pro Trinket 5V 16MHz: Trinket's got a big sister in town - the Pro Trinket 5V! Pro Trinket combines everything you love about Trinket with the familiarity of the common core Arduino chip, the ATmega328. It's like an Arduino Pro Mini with more pins and USB tossed in, so delicious. Trinket's a year old now, and while its been great to see tons of tiny projects, sometimes you just need more pins, more FLASH, and more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
  Adafruit MAX4466 Electret Microphone Amplifier: Add an ear to your project with this well-designed electret microphone amplifier. This fully assembled and tested board comes with a 20-20KHz electret microphone soldered on. For the amplification, we use the Maxim MAX4466, an op-amp specifically designed for this delicate task! The amplifier has excellent power supply noise rejection, so this amplifier sounds really good and isn't nearly as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
  Adafruit AT42QT1012 Standalone Toggle Capacitive Touch Sensor Breakout: This breakout board is the simplest way to create a project with a single "toggle" capacitive touch sensor. No microcontroller is required here - just power with 1.8 to 5.5VDC and touch the pad to activate the sensor. This sensor is a toggle output type: touch-on then touch-off. That means that when a capacitive load is detected (e.g. a person touches the sensor-pad area) the red LED will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
