# Fritzing sketch Light_blob (saved by Fritzing 0.9.3b)

parts:
  Part1 = Adafruit Pro Trinket 5V 16MHz [part_number="Adafruit #2000"]
  Part2 = NRF24L01+ Breakout Board
  VCC1 = Battery block 9V
  BAT1 = Battery Holders [package=battcom_20mm_pth]
  SP1 = SPEAKER [package=pcb_mount_speaker]
  U2 = XD-RF-5V [package=THT]
  Part3 = Adafruit MicroSD card breakout board [part_number="Adafruit #254"]
  Q1 = TRANSISTOR_NPN [package=to-92]
  U3 = WS2812 RGB LED strip
  IC1 = Voltage Regulator [package=to220-igo]
  Part4 = Adafruit Trinket 3V [part_number="Adafruit #1500"]
  BAT2 = Battery Holders [package=battcom_20mm_pth]
  R1 = Resistor [tolerance=±5% resistance=220 package="2512 [SMD]"]
  Part5 = Itsy Bitsy 32u4 5V @ 16MHz [part_number="Adafruit #3677"]

nets:
  GND: Part1.GND, VCC1.-, U2.GND, Part3.GND, Q1.E, U3.GND, IC1.IN, Part5.GND
  N1: Part1.VBAT, IC1.OUT
  VCC: Part1.+5V, SP1.-, Part3.VCC, U3.VCC, Part5.VBAT
  N2: Part1.D8, Part4.#3
  N3: Part1.D5, R1.Pin_0
  N4: Part1.D4, U3.DIN
  N5: Part1.D3, Part5.D12
  N6: Part1.D9, Part2.CE
  N7: Part1.D10, Part2.CS
  N8: Part1.D11, Part2.MOSI
  N9: Part1.D12, Part2.MISO
  N10: Part1.D13, Part2.SCK
  N11: Part2.GND, BAT1.-
  N12: Part2.VCC, BAT1.+
  N13: VCC1.+, IC1.GND
  N14: SP1.+, Q1.C
  VCC_2: U2.VCC, Part5.+5V
  N15: U2.DATA, Part5.D11
  N16: Part3.CLK, Part4.#2
  N17: Part3.DO, Part4.#1
  N18: Part3.DI, Part4.#0
  N19: Part3.CS, Part4.#4
  N20: Q1.B, R1.Pin_1
  N21: Part4.VBAT, BAT2.+
  N22: Part4.GND, BAT2.-

custom parts:
  Adafruit Pro Trinket 5V 16MHz: Trinket's got a big sister in town - the Pro Trinket 5V! Pro Trinket combines everything you love about Trinket with the familiarity of the common core Arduino chip, the ATmega328. It's like an Arduino Pro Mini with more pins and USB tossed in, so delicious. Trinket's a year old now, and while its been great to see tons of tiny projects, sometimes you just need more pins, more FLASH, and more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
  XD-RF-5V: This is 433Mhz RF transmitter with receiver kit for Arduino ARM MCU wireless Application environment: Remote control switch, receiver module, motorcycles, automobile anti-theft products, home security products, electric doors, shutter doors, windows, remote control socket, remote control LED, remote audio remote control electric doors, garage door remote control, remote control retractable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
  Adafruit MicroSD card breakout board: Not just a simple breakout board, this microSD adapter goes the extra mile - designed for ease of use. Onboard 5v->3v regulator provides 150mA for power-hungry cards 3v level shifting means you can use this with ease on either 3v or 5v systems Uses a proper level shifting chip, not resistors: less problems, and faster read/write access Use 3 or 4 digital pins to read and write 2Gb+ of storage!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
  WS2812 RGB LED strip: WS2812 strip
  Adafruit Trinket 3V: Trinket may be small, but do not be fooled by its size! It's a tiny microcontroller board, built around the Atmel ATtiny85, a little chip with a lot of power. We wanted to design a microcontroller board that was small enough to fit into any project, and low cost enough to use without hesitation. Perfect for when you don't want to give up your expensive dev-board and you aren't willing to take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
  Itsy Bitsy 32u4 5V @ 16MHz: What's smaller than a Feather but larger than a Trinket? It's an Itsy Bitsy! Small, powerful, Arduino-compatible - this microcontroller board is perfect when you want something very compact, but still with a bunch of pins. Itsy Bitsy is only 1.4" long by 0.7" wide, but has 6 power pins, 6 analog & digital pins and 17 digital pins. It packs much of the same capability as an Arduino UNO. So it's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
