# Fritzing sketch Squishee (saved by Fritzing 0.9.3b)

parts:
  J1 = Basic Force Sensing Resistor (FSR) [package=THT]
  U1 = FS1000A - 433Mhz RF Transmitter [package=THT]
  Part1 = Adafruit Trinket 3V [part_number="Adafruit #1500"]
  R1 = Resistor [tolerance=±5% resistance=10k package="2512 [SMD]"]
  BAT1 = Battery Holders [package=battcom_20mm_pth]

nets:
  N1: J1.pin_0, R1.Pin_0
  VCC: J1.pin_1, U1.VCC, Part1.+3V3
  N2: U1.DATA, Part1.#0
  GND: U1.GND, Part1.GND, Part1.#3, R1.Pin_1, BAT1.-
  N3: Part1.VBAT, BAT1.+

custom parts:
  FS1000A - 433Mhz RF Transmitter: This is 433Mhz RF transmitter with receiver kit for Arduino ARM MCU wireless Application environment: Remote control switch, receiver module, motorcycles, automobile anti-theft products, home security products, electric doors, shutter doors, windows, remote control socket, remote control LED, remote audio remote control electric doors, garage door remote control, remote control retractable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
  Adafruit Trinket 3V: Trinket may be small, but do not be fooled by its size! It's a tiny microcontroller board, built around the Atmel ATtiny85, a little chip with a lot of power. We wanted to design a microcontroller board that was small enough to fit into any project, and low cost enough to use without hesitation. Perfect for when you don't want to give up your expensive dev-board and you aren't willing to take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
