# Fritzing sketch NEW_Desk_buddy_Scheme (saved by Fritzing 0.9.3b)

parts:
  Pro_Trinket_5v = Adafruit Pro Trinket 5V 16MHz [part_number="Adafruit #2000"]
  MAX4466 = Adafruit MAX4466 Electret Microphone Amplifier [part_number="Adafruit #1063"]
  Part1 = HY-SRF05 Ultrasonic Rangefinder
  IC1 = Voltage Regulator [package=to-220-alt]
  VCC1 = Battery block 9V
  Part4 = NRF24L01+ Breakout Board
  BAT1 = Battery Holders [package=battcom_20mm_pth]
  J2 = Basic Force Sensing Resistor (FSR) [package=THT]
  R2 = Resistor [tolerance=±5% resistance=10k package="2512 [SMD]"]

nets:
  GND: Pro_Trinket_5v.GND, Pro_Trinket_5v.A1, MAX4466.GND, Part1.GND, IC1.IN, VCC1.-, R2.Pin_1
  N1: Pro_Trinket_5v.VBAT, IC1.OUT
  VCC: Pro_Trinket_5v.+5V, MAX4466.VCC, Part1.Vcc, J2.pin_1
  N2: Pro_Trinket_5v.D6, Part1.Echo
  N3: Pro_Trinket_5v.D5, Part1.Trig
  N4: Pro_Trinket_5v.D9, Part4.CS
  N5: Pro_Trinket_5v.D10, Part4.CE
  N6: Pro_Trinket_5v.D11, Part4.MOSI
  N7: Pro_Trinket_5v.D12, Part4.MISO
  N8: Pro_Trinket_5v.D13, Part4.SCK
  N9: Pro_Trinket_5v.A0, MAX4466.OUT
  N10: IC1.GND, VCC1.+
  N11: Part4.GND, BAT1.-
  N12: Part4.VCC, BAT1.+
  N13: J2.pin_0, R2.Pin_0

custom parts:
  Adafruit Pro Trinket 5V 16MHz: Trinket's got a big sister in town - the Pro Trinket 5V! Pro Trinket combines everything you love about Trinket with the familiarity of the common core Arduino chip, the ATmega328. It's like an Arduino Pro Mini with more pins and USB tossed in, so delicious. Trinket's a year old now, and while its been great to see tons of tiny projects, sometimes you just need more pins, more FLASH, and more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
  Adafruit MAX4466 Electret Microphone Amplifier: Add an ear to your project with this well-designed electret microphone amplifier. This fully assembled and tested board comes with a 20-20KHz electret microphone soldered on. For the amplification, we use the Maxim MAX4466, an op-amp specifically designed for this delicate task! The amplifier has excellent power supply noise rejection, so this amplifier sounds really good and isn't nearly as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
