# Fritzing sketch New_main_controller (saved by Fritzing 0.9.3b)

parts:
  Part1 = Adafruit Pro Trinket 5V 16MHz [part_number="Adafruit #2000"]
  Part2 = NRF24L01+ Breakout Board
  VCC1 = Battery block 9V
  BAT1 = Battery Holders [package=battcom_20mm_pth]
  SP1 = SPEAKER [package=pcb_mount_speaker]
  Part3 = Adafruit MicroSD card breakout board [part_number="Adafruit #254"]
  Q1 = TRANSISTOR_NPN [package=to-92]
  U3 = WS2812 RGB LED strip
  IC1 = Voltage Regulator [package=to220-igo]
  R1 = Resistor [tolerance=±5% resistance=220 package="2512 [SMD]"]
  Part5 = Itsy Bitsy 32u4 5V @ 16MHz [part_number="Adafruit #3677"]

nets:
  GND: Part1.GND, VCC1.-, Part3.GND, Q1.E, U3.GND, IC1.IN, Part5.GND
  N1: Part1.VBAT, IC1.OUT
  +5V: Part1.+5V, U3.VCC, Part5.VBAT
  N2: Part1.D4, U3.DIN
  N3: Part1.D3, Part5.D7
  N4: Part1.D9, Part2.CE
  N5: Part1.D10, Part2.CS
  N6: Part1.D11, Part2.MOSI
  N7: Part1.D12, Part2.MISO
  N8: Part1.D13, Part2.SCK
  N9: Part2.GND, BAT1.-
  N10: Part2.VCC, BAT1.+
  N11: VCC1.+, IC1.GND
  N12: SP1.+, Q1.C
  VCC: SP1.-, Part3.VCC, Part5.+5V
  N13: Q1.B, R1.Pin_1
  N14: R1.Pin_0, Part5.D5

notes:
  If pin 7 is HIGH then sound is speaker stops

custom parts:
  Adafruit Pro Trinket 5V 16MHz: Trinket's got a big sister in town - the Pro Trinket 5V! Pro Trinket combines everything you love about Trinket with the familiarity of the common core Arduino chip, the ATmega328. It's like an Arduino Pro Mini with more pins and USB tossed in, so delicious. Trinket's a year old now, and while its been great to see tons of tiny projects, sometimes you just need more pins, more FLASH, and more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
  Adafruit MicroSD card breakout board: Not just a simple breakout board, this microSD adapter goes the extra mile - designed for ease of use. Onboard 5v->3v regulator provides 150mA for power-hungry cards 3v level shifting means you can use this with ease on either 3v or 5v systems Uses a proper level shifting chip, not resistors: less problems, and faster read/write access Use 3 or 4 digital pins to read and write 2Gb+ of storage!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
  WS2812 RGB LED strip: WS2812 strip
  Itsy Bitsy 32u4 5V @ 16MHz: What's smaller than a Feather but larger than a Trinket? It's an Itsy Bitsy! Small, powerful, Arduino-compatible - this microcontroller board is perfect when you want something very compact, but still with a bunch of pins. Itsy Bitsy is only 1.4" long by 0.7" wide, but has 6 power pins, 6 analog & digital pins and 17 digital pins. It packs much of the same capability as an Arduino UNO. So it's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
